# Fritzing sketch WindowControllerSubsystem (saved by Fritzing 1.0.4)
breadboards: 1

parts:
  Componente1 = Arduino Uno (Rev3)
  LCD2004-I2C1 = LCD2004-I2C
  S1 = Pushbutton [package="[THT]"]
  R1 = Resistor [tolerance=±5% resistance=10k package="2010 [SMD]"]
  R2 = Trimmer Potentiometer [maximum_resistance=10kΩ knob_status=50% power=0.5W package=THT]
  J1 = Basic Servo

nets:
  N1: Componente1.A0, R2.wiper
  N2: Componente1.A1, J1.pulse
  N3: Componente1.D13/SCK, S1.Pin_3, S1.Pin_4, R1.Pin_1
  N4: Componente1.A4/SDA, LCD2004-I2C1.SDA
  N5: Componente1.A5/SCL, LCD2004-I2C1.SCL
  VCC: Componente1.5V, LCD2004-I2C1.VCC, S1.Pin_1, S1.Pin_2, R2.leg2, J1.vcc
  GND: Componente1.GND, LCD2004-I2C1.GND, R1.Pin_0, R2.leg1, J1.gnd

notes:
  Window Controller Subsystem
  - Luca Casadei 0001069237
  - Francesco Pazzaglia 0001077423

custom parts:
  LCD2004-I2C: A standard character display with 4x20 characters. Comes in many colors with LCM2004 IIC attached.
